# Fritzing sketch DroughtMonitor (saved by Fritzing 0.7.12b)

parts:
  Part1 = Arduino Prototyping Shield
  ANT1 = Antenna
  ANT2 = Antenna
  R1 = Resistor [tolerance=±5% resistance=220 package=THT]
  R2 = Resistor [tolerance=±5% resistance=220 package=THT]
  RHT1 = Humidity and Temperature Sensor RHT03
  R3 = Resistor [tolerance=±5% resistance=220 package=THT]

nets:
  +5V: Part1.+5V, RHT1.Vcc, R3.Pin_1
  N1: Part1.GND, RHT1.GND_2
  N2: Part1.D2, Part1.N$33, Part1.N$34, RHT1.Data-signal, R3.Pin_0
  N3: Part1.D6, Part1.N$76, R2.Pin_1
  N4: Part1.D7, Part1.N$118, R1.Pin_1
  N5: Part1.A0, Part1.N$178, Part1.N$190, ANT2.antenna_lead, R1.Pin_0
  N6: Part1.N$67, ANT1.antenna_lead, R2.Pin_0
